// Logisim project Extra.circ as structural Verilog: 1 circuit, main circuit main
module main (
  input  CS2,
  input  CS1,
  input  CS0,
  input  A0,
  input  A1,
  input  A2,
  input  A3,
  input  B0,
  input  B1,
  input  B2,
  input  B3,
  output V,
  output Z,
  output S4,
  output S3,
  output S2,
  output S1,
  output Cout
);

  wire n7404_1_p9, n7408_1_p1, n7408_1_p4, n7408_1_p7, n7408_1_p8, n7408_1_p11, n7408_1_p14, n7408_2_p6,
       n7408_2_p9, n7408_2_p12, n7432_2_p3, n7432_2_p6, n7486_1_p3, n7486_1_p6, n7486_1_p9, n7486_1_p12,
       n7486_2_p7, n7486_2_p9, n7486_2_p10, n7486_3_p3, n7486_3_p6, n7486_3_p9, n7486_3_p12, n74153_1_p2,
       n74153_1_p5, n74153_1_p7, n74153_1_p9, n74153_1_p12, n74153_2_p5, n74153_2_p7, n74153_2_p8,
       n74153_2_p13, n74153_2_p15, n74157_1_p1, n74157_1_p4, n74157_1_p7, n74157_1_p11, n74157_1_p14;

  // _7486 7486_1: pin names not known; wires that end beside it: B0, CS0, n7486_1_p3, B1, CS0, n7486_1_p6, B2, CS0, n7486_1_p9, B3, CS0, n7486_1_p12
  // _7408 7408_1: pin names not known; wires that end beside it: n7408_1_p1, A0, B0, n7408_1_p4, A1, B1, n7408_1_p7, n7408_1_p8, A2, B2, n7408_1_p11, A3, B3, n7408_1_p14
  // _7486 7486_2: pin names not known; wires that end beside it: CS2, 1'b1, n7408_1_p1, CS1, 1'b1, n7408_1_p8, n7486_2_p7, 1'b1, n7486_2_p9, n7486_2_p10, Cout, V
  // _7486 7486_3: pin names not known; wires that end beside it: A0, B0, n7486_3_p3, A1, B1, n7486_3_p6, A2, B2, n7486_3_p9, A3, B3, n7486_3_p12
  // _74153 74153_1: pin names not known; wires that end beside it: 1'b0, n74153_1_p2, n7486_3_p3, n7408_1_p4, n74153_1_p5, A0, n74153_1_p7, 1'b0, n74153_1_p9, n7486_3_p6, n7408_1_p7, n74153_1_p12, A1
  // _74153 74153_2: pin names not known; wires that end beside it: 1'b0, n74153_1_p2, n7486_3_p9, n7408_1_p11, n74153_2_p5, A2, n74153_2_p7, n74153_2_p8, 1'b0, n74153_1_p9, n7486_3_p12, n7408_1_p14, n74153_2_p13, A3, n74153_2_p15
  // _74157 74157_1: pin names not known; wires that end beside it: n74157_1_p1, n7486_1_p3, n7486_2_p9, n74157_1_p4, n7486_1_p6, n7486_2_p9, n74157_1_p7, 1'b0, n7486_1_p12, n7486_2_p9, n74157_1_p11, n7486_1_p9, n7486_2_p9, n74157_1_p14
  // _7408 7408_2: pin names not known; wires that end beside it: CS2, CS0, n74153_1_p9, n74153_1_p9, CS1, n7408_2_p6, CS1, n7408_1_p1, n7408_2_p9, n74153_1_p9, n7408_1_p8, n7408_2_p12
  // _7404 7404_1: pin names not known; wires that end beside it: A0, n74153_1_p5, A1, n74153_1_p12, A2, n74153_2_p5, A3, n74153_2_p13, n7404_1_p9, Z
  // _7432 7432_1: pin names not known; wires that end beside it: CS1, n74153_1_p9, n74157_1_p1, n7408_2_p9, n7408_2_p12, n74153_1_p2, n7408_1_p1, CS0, n7486_2_p7
  // _7483 7483_1: pin names not known; wires that end beside it: 1'b0, S3, n74153_2_p7, n74157_1_p14, 1'b1, S2, n74157_1_p7, n74153_2_p8, 1'b0, n7486_2_p10, n7408_2_p6, 1'b0, n74157_1_p4, n74153_1_p7, S1
  // _7483 7483_2: pin names not known; wires that end beside it: 1'b1, Cout, 1'b0, 1'b0, n7486_2_p10, 1'b0, n74157_1_p11, n74153_2_p15, S4
  // _7432 7432_2: pin names not known; wires that end beside it: S3, S4, n7432_2_p3, n7432_2_p3, S2, n7432_2_p6, n7432_2_p6, S1, n7404_1_p9

  // Notes on the sheet:
  //   Q
  //   S0
  //   Zi
  //   S1
  //   S2
  //   Cin
endmodule
